# Fritzing sketch bell (saved by Fritzing 0.9.0b)
breadboards: 1

parts:
  Part2 = Photon
  S1 = Momentary Switch [package=ksa_sealed_tac_switch]
  R1 = Resistor [tolerance=±5% resistance=220 package="1206 [SMD]"]

nets:
  N1: Part2.GND, R1.Pin_1
  N2: Part2.VIN, S1.3
  N3: Part2.D0, S1.2, R1.Pin_0
